# Fritzing sketch ckt_diag (saved by Fritzing 0.9.3b)
breadboards: 1

parts:
  Arduino_Uno = Arduino Uno (Rev3)
  Vertical_Servo_Motor = Basic Servo
  Horizontal_Servo_Motor = Basic Servo
  HC-05_Bluetooth_Module = Bluetooth HC-05 Macho
  LDR2 = Photocell (LDR) [package=THT]
  LDR3 = Photocell (LDR) [package=THT]
  LDR4 = Photocell (LDR) [package=THT]
  R1 = Resistor [tolerance=±5% resistance=10k package="0805 [SMD]"]
  R2 = Resistor [tolerance=±5% resistance=10k package="0805 [SMD]"]
  R3 = Resistor [tolerance=±5% resistance=10k package="0805 [SMD]"]
  R4 = Resistor [tolerance=±5% resistance=10k package="0805 [SMD]"]
  Solar_Panel = Solar Panel [package="Renogy 50 Watts 12 Volt Monocrystalline Bendable Solar Panel"]
  LDR1 = Photocell (LDR) [package=THT]

nets:
  N1: Arduino_Uno.A0, R1.Pin_0, LDR1.pin_0
  N2: Arduino_Uno.A1, LDR2.pin_0, R2.Pin_0
  N3: Arduino_Uno.A2, LDR3.pin_0, R3.Pin_0
  N4: Arduino_Uno.A3, LDR4.pin_0, R4.Pin_0
  N5: Arduino_Uno.A5/SCL, Solar_Panel.Connector_1
  N6: Arduino_Uno.D9_PWM, HC-05_Bluetooth_Module.RXD
  N7: Arduino_Uno.D10_PWM/SS, HC-05_Bluetooth_Module.TXD
  GND: Arduino_Uno.GND, Vertical_Servo_Motor.gnd, Horizontal_Servo_Motor.gnd, HC-05_Bluetooth_Module.GND, R1.Pin_1, R2.Pin_1, R3.Pin_1, R4.Pin_1, Solar_Panel.Connector_2
  N8: Arduino_Uno.D5_PWM, Vertical_Servo_Motor.pulse
  N9: Arduino_Uno.D6_PWM, Horizontal_Servo_Motor.pulse
  VCC: Arduino_Uno.3V3, Vertical_Servo_Motor.vcc, Horizontal_Servo_Motor.vcc, LDR2.pin_1, LDR3.pin_1, LDR4.pin_1, LDR1.pin_1
  5V: Arduino_Uno.5V, HC-05_Bluetooth_Module.VCC

custom parts:
  Solar Panel: Renogy 50 Watts 12 Volt Solar Panel
